// Logisim project TEST.circ as structural Verilog: 1 circuit, main circuit main
module main (
  input  in_1,
  output out_2,
  output [1:0] out_3,
  output game_over
);

  wire blc_rand_1_p8, clock_1_out, controlled_buffer_1_out, not_1_out;
  wire [1:0] blc_rand_1_p7;
  wire [6:0] blc_rand_1_p3;

  not not_1 (not_1_out, out_2);
  Clock clock_1 (.out(clock_1_out));
  assign controlled_buffer_1_out = not_1_out ? clock_1_out : 1'bz;  // Controlled_Buffer controlled_buffer_1
  Pull_Resistor pull_resistor_1 (.node(controlled_buffer_1_out));
  // BLC_RAND blc_rand_1: pin names not known; wires that end beside it: in_1, controlled_buffer_1_out, blc_rand_1_p3, out_3, out_2, blc_rand_1_p3, blc_rand_1_p7, blc_rand_1_p8
  Counter #(.width(1), .max('h1), .ongoal("stay")) counter_1 (
    .carry(game_over), .clk(blc_rand_1_p8));  // open: load, D, count, Q, clr
  RAM #(.addrWidth(7), .dataWidth(2), .bus("separate")) ram_1 (
    .addr(blc_rand_1_p3), .din(blc_rand_1_p7), .data(out_3), .clk(controlled_buffer_1_out));  // open: str, sel, ld, clr

  // Notes on the sheet:
  //   Daj 1 u góry, wpisz 1 w losowe miejsca w pamięci i puść zegar
endmodule
