// Logisim project main.circ as structural Verilog: 1 circuit, main circuit main
module main (
);

  wire blc_rand_1_p1, CLK, gpu_manager_1_out_5, gpu_manager_1_out_6, gpu_manager_1_out_7,
       gpu_manager_1_out_8, memoryselection_1_store_1_output, memoryselection_1_store_2_output, Selection_In,
       t_ff_1_q;
  wire [1:0] blc_rand_1_p5, Data_In, Data_Out, Gpu_Data_t, memoryselection_1_data_output_1_2,
       memoryselection_1_data_output_2_2, obnizanie_1_data_out, ram_1_data, ram_2_data, State_Select;
  wire [6:0] Adress, blc_rand_1_p4, GPU_Adress, Gpu_Adress_t, gpu_manager_1_out_4,
       memoryselection_1_adress_1_2, memoryselection_1_adress_2_2, obnizanie_1_a;
  wire [7:0] gpu_1_p5, gpu_1_p6, gpu_1_p7, gpu_1_p8, gpu_1_p9, gpu_1_p10, gpu_1_p11, gpu_1_p12, gpu_1_p13,
       gpu_1_p14, gpu_1_p15, gpu_1_p16, gpu_1_p17, gpu_1_p18, gpu_1_p19, gpu_1_p20;

  Clock clock_1 (.out(CLK));
  obnizanie obnizanie_1 (
    .A(obnizanie_1_a), .DATA_IN(Data_Out), .DATA_OUT(obnizanie_1_data_out), .CLK(CLK));  // open: ENABLE, FINISH, A1, RAM_CLK
  // BLC_RAND blc_rand_1: pin names not known; wires that end beside it: blc_rand_1_p1, blc_rand_1_p1, CLK, blc_rand_1_p4, blc_rand_1_p5
  Multiplexer #(.select(2), .width(7)) multiplexer_1 (
    .in0(obnizanie_1_a), .in2(blc_rand_1_p4), .in3(blc_rand_1_p4), .out(Adress), .sel(State_Select));  // open: in1, en
  Multiplexer #(.select(2), .width(2)) multiplexer_2 (
    .in0(obnizanie_1_data_out), .in2(blc_rand_1_p5), .in3(blc_rand_1_p5), .out(Data_In), .sel(State_Select));  // open: in1, en
  MemorySelection memoryselection_1 (
    .Adress_1(Adress), .Data_Output_1(Data_In), .Data_Output_2(2'b00), .Data_Input_1(ram_1_data),
    .Data_Input_2(ram_2_data), .Adress_2(Gpu_Adress_t), .Store_1_Input(Selection_In), .Store_2_Input(1'b0),
    .Adress_1_2(memoryselection_1_adress_1_2), .Data_Output_1_2(memoryselection_1_data_output_1_2),
    .Data_Output_2_2(memoryselection_1_data_output_2_2), .Data_Input_1_2(Data_Out),
    .Data_Input_2_2(Gpu_Data_t), .Adress_2_2(memoryselection_1_adress_2_2),
    .Store_1_Output(memoryselection_1_store_1_output), .Store_2_Output(memoryselection_1_store_2_output),
    .Select(t_ff_1_q));
  T_Flip_Flop t_ff_1 (.clk(CLK), .T(gpu_manager_1_out_8), .Q(t_ff_1_q));  // open: Qn, preset, reset, en
  Pull_Resistor pull_resistor_1 (.node(memoryselection_1_store_1_output));
  RAM #(.addrWidth(7), .dataWidth(2), .bus("separate")) ram_1 (
    .addr(memoryselection_1_adress_1_2), .din(memoryselection_1_data_output_1_2), .data(ram_1_data),
    .str(1'b1), .sel(memoryselection_1_store_1_output));  // open: clk, ld, clr
  RAM #(.addrWidth(7), .dataWidth(2), .bus("separate")) ram_2 (
    .addr(memoryselection_1_adress_2_2), .din(memoryselection_1_data_output_2_2), .data(ram_2_data),
    .str(1'b1), .sel(memoryselection_1_store_2_output));  // open: clk, ld, clr
  GPU_manager gpu_manager_1 (
    .in_1(Gpu_Data_t), .in_2(CLK), .out_3(GPU_Adress), .out_4(gpu_manager_1_out_4),
    .out_5(gpu_manager_1_out_5), .out_6(gpu_manager_1_out_6), .out_7(gpu_manager_1_out_7),
    .out_8(gpu_manager_1_out_8));
  // GPU gpu_1: pin names not known; wires that end beside it: gpu_manager_1_out_4, gpu_manager_1_out_5, gpu_manager_1_out_6, gpu_manager_1_out_7, gpu_1_p5, gpu_1_p6, gpu_1_p7, gpu_1_p8, gpu_1_p9, gpu_1_p10, gpu_1_p11, gpu_1_p12, gpu_1_p13, gpu_1_p14, gpu_1_p15, gpu_1_p16, gpu_1_p17, gpu_1_p18, gpu_1_p19, gpu_1_p20
  DotMatrix #(.inputtype("row"), .matrixcols(8), .matrixrows(16)) dotmatrix_1 (
    .row0(gpu_1_p5), .row1(gpu_1_p6), .row2(gpu_1_p7), .row3(gpu_1_p8), .row4(gpu_1_p9), .row5(gpu_1_p10),
    .row6(gpu_1_p11), .row7(gpu_1_p12), .row8(gpu_1_p13), .row9(gpu_1_p14), .row10(gpu_1_p15),
    .row11(gpu_1_p16), .row12(gpu_1_p17), .row13(gpu_1_p18), .row14(gpu_1_p19), .row15(gpu_1_p20));

  // Notes on the sheet:
  //   Ruszanie
endmodule
