// Logisim project TETRIS.circ as structural Verilog: 1 circuit, main circuit main
module main (
  input  in_1,
  input  in_2,
  input  in_3,
  output out_4
);

  wire tetris_1_p22, tetris_1_p24;
  wire [3:0] tetris_1_p1, tetris_1_p3;
  wire [6:0] tetris_1_p25;
  wire [7:0] tetris_1_p4, tetris_1_p5, tetris_1_p6, tetris_1_p7, tetris_1_p8, tetris_1_p9, tetris_1_p10,
       tetris_1_p11, tetris_1_p12, tetris_1_p13, tetris_1_p14, tetris_1_p15, tetris_1_p16, tetris_1_p17,
       tetris_1_p18, tetris_1_p19;

  Hex_Digit_Display hex_digit_display_1 (.value(tetris_1_p1));  // open: dp
  Hex_Digit_Display hex_digit_display_2 (.value(tetris_1_p3));  // open: dp
  DotMatrix #(.inputtype("row"), .matrixcols(8), .matrixrows(16)) dotmatrix_1 (
    .row0(tetris_1_p4), .row1(tetris_1_p5), .row2(tetris_1_p6), .row3(tetris_1_p7), .row4(tetris_1_p8),
    .row5(tetris_1_p9), .row6(tetris_1_p10), .row7(tetris_1_p11), .row8(tetris_1_p12), .row9(tetris_1_p13),
    .row10(tetris_1_p14), .row11(tetris_1_p15), .row12(tetris_1_p16), .row13(tetris_1_p17),
    .row14(tetris_1_p18), .row15(tetris_1_p19));
  // Tetris tetris_1: pin names not known; wires that end beside it: tetris_1_p1, in_1, tetris_1_p3, tetris_1_p4, tetris_1_p5, tetris_1_p6, tetris_1_p7, tetris_1_p8, tetris_1_p9, tetris_1_p10, tetris_1_p11, tetris_1_p12, tetris_1_p13, tetris_1_p14, tetris_1_p15, tetris_1_p16, tetris_1_p17, tetris_1_p18, tetris_1_p19, in_2, in_3, tetris_1_p22, out_4, tetris_1_p24, tetris_1_p25
  Button button_1 ();  // open: out
  Keyboard keyboard_1 (.clr(tetris_1_p22), .avail(tetris_1_p24), .data(tetris_1_p25));  // open: clk, re

  // Notes on the sheet:
  //   1. Poziom trudności
  //   2. Taktowanie
  //   3. Start
  //   Sterowanie
  //   A D - Lewo Prawo
  //   Q E - Obracanie Lewo Prawo
endmodule
