// Logisim project main.circ as structural Verilog: 1 circuit, main circuit Tetris
module Tetris (
  input  Hard,
  input  Easy,
  input  Medium,
  input  in_4,
  input  in_5,
  input  [6:0] in_6,
  output [7:0] out_7,
  output [7:0] out_8,
  output [7:0] out_9,
  output [7:0] out_10,
  output [7:0] out_11,
  output [7:0] out_12,
  output [7:0] out_13,
  output [7:0] out_14,
  output [7:0] out_15,
  output [7:0] out_16,
  output [7:0] out_17,
  output [7:0] out_18,
  output [7:0] out_19,
  output [7:0] out_20,
  output [7:0] out_21,
  output [7:0] out_22,
  output out_23
);

  wire and_1_out, blc_rand_1_game_over, blc_rand_1_out_b, CLK, clock_1_out, clock_2_out, clock_3_out,
       comparator_1_gt, comparator_1_lt, comparator_3_eq, comparator_3_gt, comparator_3_lt, comparator_4_eq,
       comparator_5_eq, comparator_6_eq, comparator_6_gt, comparator_6_lt, comparator_7_eq, d_ff_3_q,
       deleting_rows_1_out_5, Deleting_Rows_CLK, demultiplexer_2_out0, demultiplexer_2_out1,
       demultiplexer_3_out0, demultiplexer_3_out1, demultiplexer_4_out0, demultiplexer_4_out1, Game_CLK,
       Game_over, gpu_manager_1_out_6, gpu_manager_1_out_7, gpu_manager_1_out_8, gpu_manager_1_out_9,
       keyboard_manager_1_out_6, main_1_finish, main_1_ram_clk, main_1_zderzenie, main_2_finish,
       main_2_ram_clk, main_2_zd, main_3_finish, main_3_ram_clk, main_3_zd, main_4_flaga, main_4_flaga_2,
       main_4_trwajaca_akcja, multiplexer_8_out, or_1_out, or_2_out, or_3_out, or_4_out, or_5_out, or_6_out,
       pull_resistor_1_node, pull_resistor_2_node, pull_resistor_6_node, RAM_CLK;
  wire [1:0] blc_rand_1_out_d, comparator_2_eq, counter_1_q, Data_In, Data_Out, Deleting_Rows_Data_In,
       Deleting_Rows_Data_Out, demultiplexer_1_out2, demultiplexer_1_out4, Game_Data, Game_Data_In, Gpu_Data,
       main_1_data_out, main_2_data_out, main_3_data_out;
  wire [2:0] State_Select;
  wire [3:0] Score;
  wire [6:0] Adress, blc_rand_1_out_a, Deleting_Rows_Adress, Game_Adress, GPU_Adress, gpu_manager_1_out_5,
       keyboard_manager_1_out_4, main_1_a, main_1_nowe_a1, main_2_a, main_2_nowe_a1, main_3_a,
       multiplexer_1_out, register_1_q;

  Demultiplexer #(.select(3), .width(2)) demultiplexer_1 (
    .out1(Gpu_Data), .out2(demultiplexer_1_out2), .out3(Game_Data), .out4(demultiplexer_1_out4),
    .out5(Deleting_Rows_Data_In), .in(Data_Out), .sel(State_Select));  // open: out0, out6, out7, en
  Comparator #(.width(3), .mode("unsigned")) comparator_1 (
    .a(State_Select), .b(3'b011), .gt(comparator_1_gt), .eq(comparator_2_eq[1]), .lt(comparator_1_lt));
  or or_1 (or_1_out, comparator_1_gt, comparator_1_lt);
  Multiplexer #(.select(2), .width(7), .enable("false")) multiplexer_1 (
    .in0(main_1_nowe_a1), .in1(7'b0000010), .in2(main_2_nowe_a1), .in3(main_2_nowe_a1),
    .out(multiplexer_1_out), .sel(comparator_2_eq));
  Register #(.width(7)) register_1 (.D(multiplexer_1_out), .Q(register_1_q), .clk(or_2_out));  // open: en, clr
  or or_2 (or_2_out, blc_rand_1_out_b, main_2_finish, main_1_finish);
  Comparator #(.width(3), .mode("unsigned")) comparator_2 (
    .a(State_Select), .b(3'b100), .eq(comparator_2_eq[0]));  // open: gt, lt
  Comparator #(.width(3), .mode("unsigned")) comparator_3 (
    .a(State_Select), .b(3'b010), .gt(comparator_3_gt), .eq(comparator_3_eq), .lt(comparator_3_lt));
  Comparator #(.width(3), .mode("unsigned")) comparator_4 (
    .a(State_Select), .b(3'b101), .eq(comparator_4_eq));  // open: gt, lt
  Pull_Resistor pull_resistor_1 (.node(pull_resistor_1_node));
  T_Flip_Flop t_ff_1 (.clk(CLK), .T(1'b1), .Q(pull_resistor_1_node), .reset(or_1_out));  // open: Qn, preset, en
  Pull_Resistor pull_resistor_2 (.node(pull_resistor_2_node));
  T_Flip_Flop t_ff_2 (.clk(CLK), .T(1'b1), .Q(pull_resistor_2_node), .reset(or_3_out));  // open: Qn, preset, en
  or or_3 (or_3_out, comparator_3_gt, comparator_3_lt);
  Demultiplexer demultiplexer_2 (
    .out0(demultiplexer_2_out0), .out1(demultiplexer_2_out1), .in(pull_resistor_1_node),
    .sel(main_4_trwajaca_akcja));  // open: en
  Demultiplexer demultiplexer_3 (
    .out0(demultiplexer_3_out0), .out1(demultiplexer_3_out1), .in(comparator_2_eq[1]),
    .sel(main_4_trwajaca_akcja));  // open: en
  D_Flip_Flop d_ff_1 (.clk(comparator_2_eq[0]), .D(1'b1));  // open: Q, Qn, preset, en, reset
  BLC_RAND blc_rand_1 (
    .CLK(CLK), .OUT_A(blc_rand_1_out_a), .OUT_D(blc_rand_1_out_d), .START(comparator_2_eq[0]),
    .OUT_B(blc_rand_1_out_b), .CURRENT_GAME_ADRESS(blc_rand_1_out_a),
    .CURRENT_GAME_STATE(demultiplexer_1_out4), .GAME_OVER(blc_rand_1_game_over));
  opadanie_main main_1 (
    .A1(register_1_q), .DATA_IN(demultiplexer_1_out2), .CLK(pull_resistor_2_node), .ENABLE(comparator_3_eq),
    .DATA_OUT(main_1_data_out), .A(main_1_a), .RAM_CLK(main_1_ram_clk), .FINISH(main_1_finish),
    .ZDERZENIE(main_1_zderzenie), .RESET(or_3_out), .NOWE_A1(main_1_nowe_a1));
  Pull_Resistor pull_resistor_3 (.node(or_3_out));
  Deleting_Rows deleting_rows_1 (
    .FROM_RAM_D(Deleting_Rows_Data_In), .If_1_enables_circuit(comparator_4_eq), .CLK_input(CLK),
    .out_5(deleting_rows_1_out_5), .TO_RAM_adress(Deleting_Rows_Adress), .TO_RAM_D(Deleting_Rows_Data_Out),
    .TO_RAM_CLK(Deleting_Rows_CLK), .Score(Score));
  Multiplexer #(.width(7)) multiplexer_2 (
    .in0(main_3_a), .in1(main_2_a), .out(Game_Adress), .sel(main_4_trwajaca_akcja));  // open: en
  Pull_Resistor pull_resistor_4 (.node(or_1_out));
  Pull_Resistor pull_resistor_5 (.node(or_1_out));
  D_Flip_Flop d_ff_2 (.clk(blc_rand_1_game_over), .D(1'b1), .Q(Game_over));  // open: Qn, preset, en, reset
  and and_1 (and_1_out, main_1_finish, main_1_zderzenie);
  D_Flip_Flop d_ff_3 (.clk(and_1_out), .D(1'b1), .Q(d_ff_3_q), .reset(comparator_5_eq));  // open: Qn, preset, en
  Comparator #(.width(3), .mode("unsigned")) comparator_5 (
    .a(State_Select), .b(3'b100), .eq(comparator_5_eq));  // open: gt, lt
  Demultiplexer #(.disabled(0), .enable("false")) demultiplexer_4 (
    .out0(demultiplexer_4_out0), .out1(demultiplexer_4_out1), .in(main_1_finish), .sel(comparator_6_eq));
  przesuwanie_main main_2 (
    .A1(register_1_q), .CLK(demultiplexer_2_out1), .ENABLE(demultiplexer_3_out1), .DATA_IN(Game_Data),
    .FLAGA(main_4_flaga), .NOWE_A1(main_2_nowe_a1), .DATA_OUT(main_2_data_out), .RAM_CLK(main_2_ram_clk),
    .ZD(main_2_zd), .A(main_2_a), .FINISH(main_2_finish), .RESET(or_1_out));
  rotacja_main main_3 (
    .A1(register_1_q), .CLK(demultiplexer_2_out0), .ENABLE(demultiplexer_3_out0), .DATA_IN(Game_Data),
    .FLAGA(main_4_flaga_2), .DATA_OUT(main_3_data_out), .RAM_CLK(main_3_ram_clk), .ZD(main_3_zd),
    .A(main_3_a), .FINISH(main_3_finish), .RESET(or_1_out));
  Multiplexer #(.select(3), .width(7)) multiplexer_3 (
    .in1(GPU_Adress), .in2(main_1_a), .in3(Game_Adress), .in4(blc_rand_1_out_a), .in5(Deleting_Rows_Adress),
    .out(Adress), .sel(State_Select));  // open: in0, in6, in7, en
  Counter #(.width(2), .max('h3)) counter_1 (
    .Q(counter_1_q), .clk(pull_resistor_6_node), .clr(comparator_5_eq));  // open: load, D, count, carry
  Pull_Resistor pull_resistor_6 (.node(pull_resistor_6_node));
  assign pull_resistor_6_node = d_ff_3_q ? main_1_finish : 1'bz;  // Controlled_Buffer controlled_buffer_1
  Multiplexer multiplexer_4 (
    .in0(main_3_ram_clk), .in1(main_2_ram_clk), .out(Game_CLK), .sel(main_4_trwajaca_akcja));  // open: en
  Multiplexer #(.width(2)) multiplexer_5 (
    .in0(main_3_data_out), .in1(main_2_data_out), .out(Game_Data_In), .sel(main_4_trwajaca_akcja));  // open: en
  Multiplexer #(.select(3), .width(2)) multiplexer_6 (
    .in2(main_1_data_out), .in3(Game_Data_In), .in4(blc_rand_1_out_d), .in5(Deleting_Rows_Data_Out),
    .out(Data_In), .sel(State_Select));  // open: in0, in1, in6, in7, en
  Multiplexer #(.select(3)) multiplexer_7 (
    .in2(main_1_ram_clk), .in3(Game_CLK), .in4(CLK), .in5(Deleting_Rows_CLK), .out(RAM_CLK),
    .sel(State_Select));  // open: in0, in1, in6, in7, en
  Comparator #(.width(2), .mode("unsigned")) comparator_6 (
    .a(counter_1_q), .b(2'b11), .gt(comparator_6_gt), .eq(comparator_6_eq), .lt(comparator_6_lt));
  or or_4 (or_4_out, in_4, demultiplexer_4_out1);
  Keyboard_Manager keyboard_manager_1 (
    .out_4(keyboard_manager_1_out_4), .out_5(out_23), .in_2(in_5), .in_1(in_6),
    .out_6(keyboard_manager_1_out_6), .in_3(or_5_out));
  or or_5 (or_5_out, main_2_finish, main_3_finish);
  Clock #(.highDuration(4), .lowDuration(4)) clock_1 (.out(clock_1_out));
  Clock #(.highDuration(2), .lowDuration(2)) clock_2 (.out(clock_2_out));
  Clock clock_3 (.out(clock_3_out));
  State_Selector state_selector_1 (
    .Keyboard__Input_Happened(keyboard_manager_1_out_6), .out_9(State_Select), .New_Block_Request(or_4_out),
    .Generating_Ended(blc_rand_1_out_b), .Falling_Ended(demultiplexer_4_out0), .Player_Input_Ended(or_6_out),
    .Render(gpu_manager_1_out_9), .Deleting_Rows_Ended(deleting_rows_1_out_5), .GO(Game_over));
  Multiplexer multiplexer_8 (
    .in0(main_3_zd), .in1(main_2_zd), .out(multiplexer_8_out), .sel(main_4_trwajaca_akcja));  // open: en
  Multiplexer #(.select(3), .disabled(0)) multiplexer_9 (
    .in1(clock_1_out), .in2(clock_2_out), .in4(clock_3_out), .out(CLK), .sel({Hard, Medium, Easy}));  // open: in0, in3, in5, in6, in7, en
  or or_6 (or_6_out, main_3_finish, main_2_finish);
  koder_klawiatura_main main_4 (
    .wejscie_ASCI(keyboard_manager_1_out_4), .FLAGA(main_4_flaga), .FLAGA_2(main_4_flaga_2),
    .TRWAJACA_AKCJA(main_4_trwajaca_akcja));
  Comparator #(.width(3), .mode("unsigned")) comparator_7 (
    .a(State_Select), .b(3'b001), .eq(comparator_7_eq));  // open: gt, lt
  GPU_manager gpu_manager_1 (
    .in_1(Gpu_Data), .out_4(GPU_Adress), .out_5(gpu_manager_1_out_5), .out_6(gpu_manager_1_out_6),
    .out_7(gpu_manager_1_out_7), .out_8(gpu_manager_1_out_8), .out_9(gpu_manager_1_out_9),
    .ENABLE(comparator_7_eq), .in_3(CLK));
  RAM #(.addrWidth(7), .dataWidth(2), .bus("separate")) ram_1 (
    .addr(Adress), .din(Data_In), .data(Data_Out), .clk(RAM_CLK));  // open: str, sel, ld, clr
  GPU gpu_1 (
    .in_2(gpu_manager_1_out_5), .in_4(gpu_manager_1_out_6), .in_5(gpu_manager_1_out_7),
    .in_6(gpu_manager_1_out_8), .out_7(out_7), .out_8(out_8), .out_9(out_9), .out_10(out_10),
    .out_11(out_11), .out_12(out_12), .out_13(out_13), .out_14(out_14), .out_15(out_15), .out_16(out_16),
    .out_17(out_17), .out_18(out_18), .out_19(out_19), .out_20(out_20), .out_21(out_21), .out_22(out_22),
    .Score(Score), .Game_Over(Game_over));

  // Notes on the sheet:
  //   ten finisz wystepuje ale od razu sie gasi, bo resetuje tez koder i zmienia flage akcji
endmodule
